# Fritzing sketch PortalSketch (saved by Fritzing 1.0.6)
circuit board: 7.10028cm x 9.68483cm
breadboards: 2

parts:
  DFRobot_DFPlayer_Mini1 = DFRobot DFPlayer Mini [part_number=DFR0299]
  DFRobot_DFPlayer_Mini2 = DFRobot DFPlayer Mini [part_number=DFR0299]
  R1 = Resistor [tolerance=±5% power=0.25W resistance=220 package=THT]
  S1 = Round Pushbutton
  S2 = Round Pushbutton
  SP1 = SPEAKER [package=pcb_mount_speaker]
  SP2 = SPEAKER [package=pcb_mount_speaker]
  Part2 = 12 NeoPixel Ring [part_number=1643]
  Part3 = NeoPixel Jewel [part_number=2226]
  Part4 = Adafruit Breadboard-Friendly NeoPixel [part_number="Adafruit #1312"]
  Part5 = Adafruit Breadboard-Friendly NeoPixel [part_number="Adafruit #1312"]
  Part6 = Adafruit Breadboard-Friendly NeoPixel [part_number="Adafruit #1312"]
  U2 = LuaNode32 / ESP32 [part_number=ESP32S-PIN30]
  Grove1 = Grove OLED 128x96
  RE1 = KY-040 Rotary encoder [package=THT]
  Part7 = TXB0108 8-channel Bi-directional Logic Level Converter
  C1 = Electrolytic Capacitor [capacitance=100µF voltage=35V package="200 mil [THT, electrolytic]"]
  C2 = Electrolytic Capacitor [capacitance=100µF voltage=35V package="200 mil [THT, electrolytic]"]

nets (from the breadboard view):
  VDD: DFRobot_DFPlayer_Mini1.VCC, DFRobot_DFPlayer_Mini2.VCC, Part2.VDD, Part3.VDD, Part4.VDD, Part5.VDD, Part6.VDD, U2.Vin, Part7.VCCB, C2.-
  N1: DFRobot_DFPlayer_Mini1.RX, U2.D27
  N2: DFRobot_DFPlayer_Mini1.TX, U2.D26
  N3: DFRobot_DFPlayer_Mini1.SPK_1, SP2.+
  GND: DFRobot_DFPlayer_Mini1.GND-1, DFRobot_DFPlayer_Mini1.GND-2, DFRobot_DFPlayer_Mini2.GND-1, DFRobot_DFPlayer_Mini2.GND-2, S1.leg1, S2.leg1, Part2.GND, Part3.GND, Part4.GND, Part5.GND, Part6.GND, U2.GND, Grove1.GND, RE1.GND, Part7.GND, C1.+, C2.+
  N4: DFRobot_DFPlayer_Mini1.SPK_2, SP2.-
  N5: DFRobot_DFPlayer_Mini2.RX, U2.RX2
  N6: DFRobot_DFPlayer_Mini2.TX, U2.TX2
  N7: DFRobot_DFPlayer_Mini2.SPK_1, SP1.+
  N8: DFRobot_DFPlayer_Mini2.SPK_2, SP1.-
  N9: R1.Pin_0, Part7.B1
  N10: R1.Pin_1, Part6.IN
  N11: S1.leg0, U2.D25
  N12: S2.leg0, U2.D33
  N13: Part2.IN, Part5.OUT
  N14: Part2.OUT, Part3.IN
  N15: Part4.IN, Part6.OUT
  N16: Part4.OUT, Part5.IN
  N17: U2.D34, RE1.CLK
  N18: U2.D35, RE1.DT
  N19: U2.D32, RE1.SW
  3V3: U2.3V3, RE1.Vcc, Part7.VCCA, C1.-
  N20: U2.D19, Part7.A1
  N21: U2.D21, Grove1.SDA
  N22: U2.D22, Grove1.SCL

notes:
  5V
  3v3
  bg sfx
  portal sfx

custom parts:
  12 NeoPixel Ring: 12 ultra bright smart LED NeoPixels are arranged in a circle with 1.5" (37mm) outer diameter. The rings are 'chainable' - connect the output pin of one to the input pin of another. Use only one microcontroller pin to control as many as you can chain together! Each LED is addressable as the driver chip is inside the LED. Each one has ~18mA constant current drive so the color will be very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
  NeoPixel Jewel: We fit seven of our tiny 5050 (5mm x 5mm) smart RGB LEDs onto a beautiful, round PCB with mounting holes and a chainable design to create what we think is our most elegant (and evening-wear appropriate) NeoPixel board yet. Use only one microcontroller pin to control as many as you can chain together! Each LED is addressable as the driver chip is inside the LED. Each one has ~18mA constant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
  Adafruit Breadboard-Friendly NeoPixel: This is the easiest way possible to add small, bright RGB pixels to your project. We took the same technology from our Flora NeoPixels and made them breadboard friendly, with two rows of 3 x 0.1" spaced header on each side for easy soldering, chaining and breadboarding. These ultra-bright LEDs have a constant-current driver cooked right into the LED package! The pixels are chainable - so you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
  LuaNode32 / ESP32: New Image for LuaNode32 DOIT ESP32 DEVKIT V1. Base parts from LuaNode32 / ESP32 ESP32 based LuaNode32 by G.Noorlander DOIT Esp32 DevKit v1 (30 pins long, 11 pins width) by Werner Rothschopf (modified by vanepp Dec 2018)
  KY-040 Rotary encoder: KY-040 Rotary Encoder with switch on breakout borad from AZ Delivery
  TXB0108 8-channel Bi-directional Logic Level Converter: Because the Arduino (and Basic Stamp) are 5V devices, and most modern sensors, displays, flash cards and modes are 3.3V-only, many makers find that they need to perform level shifting/conversion to protect the 3.3V device from 5V. Although one can use resistors to make a divider, for high speed transfers, the resistors can add a lot of slew and cause havoc that is tough to debug. For that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
